// Logisim project lab3-variant7.circ as structural Verilog: 1 circuit, main circuit main
module main (
  input  \_2_бит ,
  input  \_1_бит ,
  input  \_0_бит ,
  output \_2_бит_2 ,
  output \_1_бит_2 ,
  output \_0_бит_2 ,
  output out_7,
  output out_8,
  output out_9,
  output out_10,
  output out_11,
  output out_12,
  output out_13
);

  wire and_1_out, and_2_out, and_3_out, and_4_out, and_5_out, and_6_out, and_7_out, and_8_out, and_9_out,
       and_10_out, and_11_out, and_12_out, and_13_out, and_14_out, and_15_out, not_1_out, not_2_out,
       not_3_out;

  not not_1 (not_1_out, \_2_бит );
  not not_2 (not_2_out, \_1_бит );
  not not_3 (not_3_out, \_0_бит );
  and and_1 (and_1_out, not_1_out, not_2_out, \_0_бит );
  and and_2 (and_2_out, \_2_бит , \_1_бит , \_0_бит );
  and and_3 (and_3_out, not_1_out, \_1_бит );
  and and_4 (and_4_out, \_2_бит , not_2_out);
  and and_5 (and_5_out, \_2_бит , not_3_out);
  and and_6 (and_6_out, \_2_бит , not_2_out, \_0_бит );
  and and_7 (and_7_out, \_2_бит , \_1_бит , not_3_out);
  and and_8 (and_8_out, \_2_бит , \_1_бит , \_0_бит );
  and and_9 (and_9_out, not_1_out, not_2_out, not_3_out);
  and and_10 (and_10_out, not_1_out, not_2_out, \_0_бит );
  and and_11 (and_11_out, not_1_out, \_1_бит , not_3_out);
  and and_12 (and_12_out, not_1_out, \_1_бит , \_0_бит );
  and and_13 (and_13_out, \_2_бит , not_2_out, not_3_out);
  and and_14 (and_14_out, \_2_бит , not_2_out, \_0_бит );
  and and_15 (and_15_out, \_2_бит , \_1_бит , not_3_out);
  or or_1 (\_2_бит_2 , and_1_out, and_2_out);
  or or_2 (\_1_бит_2 , and_3_out, and_4_out, and_5_out);
  or or_3 (\_0_бит_2 , and_6_out, and_7_out);
  or or_4 (out_7, and_8_out, and_9_out);
  or or_5 (out_8, and_8_out, and_10_out);
  or or_6 (out_9, and_8_out, and_11_out);
  or or_7 (out_10, and_8_out, and_12_out);
  or or_8 (out_11, and_8_out, and_13_out);
  or or_9 (out_12, and_8_out, and_14_out);
  or or_10 (out_13, and_8_out, and_15_out);
endmodule
