// Logisim project lab4.circ as structural Verilog: 1 circuit, main circuit main
module main (
  input  R,
  input  S,
  input  S_2,
  input  R_2,
  input  S_3,
  input  C,
  input  R_3,
  input  S_4,
  input  R_4,
  input  S_5,
  input  R_5,
  input  S_6,
  input  R_6,
  output Q,
  output notQ,
  output Q_2,
  output notQ_2,
  output Q_3,
  output notQ_3,
  output Q_4,
  output notQ_4,
  output Q_5,
  output notQ_5,
  output Q_6,
  output notQ_6
);

  wire nand_3_out, nand_4_out, nand_5_out, nand_6_out, nand_7_out, nand_8_out, nand_9_out, nand_10_out,
       nand_17_out, nand_18_out;

  nor nor_1 (Q, R, notQ);
  nor nor_2 (notQ, Q, S);
  nand nand_1 (Q_2, S_2, notQ_2);
  nand nand_2 (notQ_2, Q_2, R_2);
  nand nand_3 (nand_3_out, S_3, C);
  nand nand_4 (nand_4_out, C, R_3);
  nand nand_5 (nand_5_out, S_4, S_4);
  nand nand_6 (nand_6_out, nand_5_out, R_4);
  nand nand_7 (nand_7_out, S_5, nand_8_out);
  nand nand_8 (nand_8_out, R_5, R_5);
  nand nand_9 (nand_9_out, S_6, S_6);
  nand nand_10 (nand_10_out, R_6, R_6);
  nand nand_11 (Q_3, nand_3_out, notQ_3);
  nand nand_12 (notQ_3, Q_3, nand_4_out);
  nand nand_13 (Q_4, nand_5_out, notQ_4);
  nand nand_14 (notQ_4, Q_4, nand_6_out);
  nand nand_15 (Q_5, nand_7_out, notQ_5);
  nand nand_16 (notQ_5, Q_5, nand_8_out);
  nand nand_17 (nand_17_out, S_6, nand_10_out);
  nand nand_18 (nand_18_out, nand_9_out, R_6);
  nand nand_19 (Q_6, nand_17_out, notQ_6);
  nand nand_20 (notQ_6, Q_6, nand_18_out);

  // Notes on the sheet:
  //   S-триггер
  //   R-триггер
  //   E-триггер
  //   Синхронный RS триггер
  //   Асинхронный RS триггер с прямыми входами
  //   Асинхронный  RS триггер с инверсивными входами
endmodule
