// Logisim project lab5-test.circ as structural Verilog: 1 circuit, main circuit main
module main (
  input  J,
  input  C,
  input  K,
  output out_4,
  output out_5
);

  wire nand_1_out, nand_2_out, nand_3_out, nand_4_out, nand_5_out, nand_6_out;

  nand nand_1 (nand_1_out, out_5, J, C);
  nand nand_2 (nand_2_out, C, K, out_4);
  nand nand_3 (nand_3_out, nand_1_out, nand_4_out);
  nand nand_4 (nand_4_out, nand_3_out, nand_2_out);
  nand nand_5 (nand_5_out, nand_1_out, nand_3_out);
  nand nand_6 (nand_6_out, nand_4_out, nand_2_out);
  nand nand_7 (out_4, nand_5_out, out_5);
  nand nand_8 (out_5, out_4, nand_6_out);

  // Notes on the sheet:
  //   D-триггер
  //   JK-триггер
endmodule
