// Logisim project lab5.circ as structural Verilog: 1 circuit, main circuit main
module main (
  input  D,
  input  C,
  input  in_3,
  input  T,
  input  C_2,
  input  J,
  input  C_3,
  input  K,
  output Q,
  output notQ,
  output Q_2,
  output notQ_2,
  output out_13,
  output out_14
);

  wire nand_1_out, nand_2_out, nand_3_out, nand_4_out, nand_5_out, nand_6_out, nand_7_out, nand_8_out,
       nand_9_out, nand_14_out, nand_15_out;

  nand nand_1 (nand_1_out, T, C_2);
  nand nand_2 (nand_2_out, D, C);
  nand nand_3 (nand_3_out, nand_2_out, C);
  nand nand_4 (nand_4_out, out_14, J, C_3);
  nand nand_5 (nand_5_out, C_3, K, out_13);
  nand nand_6 (nand_6_out, in_3, nand_1_out);
  nand nand_7 (nand_7_out, nand_6_out, nand_1_out);
  nand nand_8 (nand_8_out, nand_4_out, nand_9_out);
  nand nand_9 (nand_9_out, nand_8_out, nand_5_out);
  nand nand_10 (Q, nand_2_out, notQ);
  nand nand_11 (notQ, Q, nand_3_out);
  nand nand_12 (Q_2, nand_6_out, notQ_2);
  nand nand_13 (notQ_2, Q_2, nand_7_out);
  nand nand_14 (nand_14_out, nand_4_out, nand_8_out);
  nand nand_15 (nand_15_out, nand_9_out, nand_5_out);
  nand nand_16 (out_13, nand_14_out, out_14);
  nand nand_17 (out_14, out_13, nand_15_out);

  // Notes on the sheet:
  //   D-триггер
  //   T-триггер
  //   JK-триггер
endmodule
