// Logisim project lab6.circ as structural Verilog: 6 circuits, main circuit main
module main (
  input  X1,
  input  X2,
  output Y
);

  wire and_1_out, and_2_out, not_1_out, not_2_out;

  not not_1 (not_1_out, X1);
  not not_2 (not_2_out, X2);
  and and_1 (and_1_out, not_1_out, X2);
  and and_2 (and_2_out, X1, not_2_out);
  or or_1 (Y, and_1_out, and_2_out);
endmodule

module \полусумматор  (
  input  X1,
  input  X2,
  output \Старший_разряд ,
  output \Младший_разряд 
);

  main main_1 (.X1(X1), .X2(X2), .Y(\Младший_разряд ));
  and and_1 (\Старший_разряд , X1, X2);
endmodule

module \полный_сумматор  (
  input  X1,
  input  X2,
  input  Pi,
  output P,
  output S
);

  wire \полусумматор_1_младший_разряд , \полусумматор_1_старший_разряд , \полусумматор_2_старший_разряд ;

  \полусумматор  \u_полусумматор_1  (
    .X1(X1), .X2(X2), .\Старший_разряд (\полусумматор_1_старший_разряд ),
    .\Младший_разряд (\полусумматор_1_младший_разряд ));
  \полусумматор  \u_полусумматор_2  (
    .X1(\полусумматор_1_младший_разряд ), .X2(Pi), .\Старший_разряд (\полусумматор_2_старший_разряд ),
    .\Младший_разряд (S));
  or or_1 (P, \полусумматор_1_старший_разряд , \полусумматор_2_старший_разряд );
endmodule

module \_4сумматора  (
  input  X4,
  input  Y4,
  input  X3,
  input  Y3,
  input  X2,
  input  Y2,
  input  X1,
  input  Y1,
  input  P0,
  output S5,
  output S4,
  output S3,
  output S2,
  output S1
);

  wire \полный_сумматор_1_p , \полный_сумматор_2_p , \полный_сумматор_3_p ;

  \полный_сумматор  \u_полный_сумматор_1  (.X1(X1), .X2(Y1), .Pi(P0), .P(\полный_сумматор_1_p ), .S(S1));
  \полный_сумматор  \u_полный_сумматор_2  (
    .X1(X2), .X2(Y2), .Pi(\полный_сумматор_1_p ), .P(\полный_сумматор_2_p ), .S(S2));
  \полный_сумматор  \u_полный_сумматор_3  (
    .X1(X3), .X2(Y3), .Pi(\полный_сумматор_2_p ), .P(\полный_сумматор_3_p ), .S(S3));
  \полный_сумматор  \u_полный_сумматор_4  (.X1(X4), .X2(Y4), .Pi(\полный_сумматор_3_p ), .P(S5), .S(S4));
endmodule

module \полусумматор_теория  (
  input  A,
  input  B,
  output S,
  output P
);

  wire not_1_out, or_1_out;

  or or_1 (or_1_out, A, B);
  and and_1 (P, A, B);
  not not_1 (not_1_out, P);
  and and_2 (S, or_1_out, not_1_out);
endmodule

module \полный_сумматор_теория  (
  input  A,
  input  B,
  input  P0,
  output P,
  output S
);

  wire and_1_out, and_2_out, and_3_out, and_4_out, and_5_out, not_1_out, or_1_out;

  and and_1 (and_1_out, A, B);
  and and_2 (and_2_out, A, P0);
  and and_3 (and_3_out, B, P0);
  or or_1 (or_1_out, A, B, P0);
  and and_4 (and_4_out, A, B, P0);
  or or_2 (P, and_1_out, and_2_out, and_3_out);
  not not_1 (not_1_out, P);
  and and_5 (and_5_out, not_1_out, or_1_out);
  or or_3 (S, and_5_out, and_4_out);
endmodule
